# Fritzing sketch arduino_IR_Diagram (saved by Fritzing 0.7.5b)
breadboards: 1

parts:
  Arduino1 = Arduino
  LED1 = LED - 5mm [color="Infrared (940nm)" package="5 mm [THT]"]
  R1 = Resistor [tolerance=±5% resistance=220 package=THT]
  LED2 = LED - 5mm [color="Red (633nm)" package="5 mm [THT]"]  # not connected
  R2 = Resistor [tolerance=±5% resistance=220 package=THT]
  S1 = Pushbutton [package="[THT]"]

nets:
  N1: Arduino1.D9, R2.Pin_0
  N2: Arduino1.D3, R1.Pin_0
  N3: Arduino1.D2, S1.Pin_3, S1.Pin_4
  N4: Arduino1.GND, LED1.anode
  N5: LED1.cathode, R1.Pin_1
  N6: S1.Pin_1, S1.Pin_2
